# Fritzing sketch scheme (saved by Fritzing 0.9.3b)
perfboards: 1

parts:
  SparkFun_ESP32_Thing1 = SparkFun ESP32 Thing [part_number=DEV-13907]
  S2 = Pushbutton [package="[SMD]"]
  S3 = Pushbutton [package="[SMD]"]
  U4 = SWITCH_SPDT [package=kps-1290]
  U5 = SWITCH_SPDT [package=kps-1290]
  U6 = SWITCH_SPDT [package=kps-1290]
  U7 = SWITCH_SPDT [package=kps-1290]
  U8 = SWITCH_SPDT [package=kps-1290]
  U9 = SWITCH_SPDT [package=kps-1290]
  R1 = Resistor [tolerance=±5% resistance=1M package="0402 [SMD]"]
  R2 = Resistor [tolerance=±5% resistance=1M package="0402 [SMD]"]
  R3 = Resistor [tolerance=±5% resistance=1M package="0402 [SMD]"]
  R4 = Resistor [tolerance=±5% resistance=1M package="0402 [SMD]"]

nets:
  GND: SparkFun_ESP32_Thing1.GND, S2.Pin_4, S3.Pin_3, R3.Pin_1, R4.Pin_1
  3.3V: SparkFun_ESP32_Thing1.3.3V, R1.Pin_1, R2.Pin_1
  N1: SparkFun_ESP32_Thing1.CHIP_PU, S3.Pin_1
  N2: SparkFun_ESP32_Thing1.27, U9.P
  N3: SparkFun_ESP32_Thing1.34, U8.P
  N4: SparkFun_ESP32_Thing1.32K_XP, U7.P
  N5: SparkFun_ESP32_Thing1.0, S2.Pin_1, S2.Pin_2
  N6: SparkFun_ESP32_Thing1.2, U6.P
  N7: SparkFun_ESP32_Thing1.23, U4.P
  N8: SparkFun_ESP32_Thing1.22, U5.P
  N9: U4.O, U5.O, U6.O, R4.Pin_0
  N10: U4.S, U5.S, U6.S, R2.Pin_0
  N11: U7.O, U8.O, U9.O, R3.Pin_0
  N12: U7.S, U8.S, U9.S, R1.Pin_0

custom parts:
  SparkFun ESP32 Thing: The SparkFun ESP32 Thing is a comprehensive development platform for Espressif’s ESP32, their super-charged version of the popular ESP8266. Like the 8266, the ESP32 is a WiFi-compatible microcontroller, but to that it adds support for Bluetooth low-energy (i.e BLE, BT4.0, Bluetooth Smart), and nearly 30 I/O pins. The ESP32’s power and versatility will make it the foundation of IoT and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
